# Fritzing sketch DistanceAlarm (saved by Fritzing 0.9.5d)
breadboards: 1

parts:
  HC-SR04_Sensor_1 = HC-SR04 Ultrasonic Distance Sensor
  J1 = Piezo Speaker
  Mod1 = Raspberry Pi Pico W
  R1 = Resistor [tolerance=±5% resistance=220 package=THT]
  LED1 = LED - 3mm [color="Red (633nm)" package="3 mm [THT]"]  # not connected
  LED2 = LED - 3mm [color="Green (555nm)" package="3 mm [THT]"]
  R2 = Resistor [tolerance=±5% resistance=220 package=THT]

nets:
  N1: HC-SR04_Sensor_1.VCC, Mod1.pin_40
  N2: HC-SR04_Sensor_1.TRIG, Mod1.pin_22
  N3: HC-SR04_Sensor_1.ECHO, Mod1.pin_21
  N4: HC-SR04_Sensor_1.GND, J1.pin1, Mod1.pin_3, Mod1.pin_8, Mod1.pin_13, Mod1.pin_18, Mod1.pin_23, Mod1.pin_28, Mod1.pin_33, Mod1.pin_38, Mod1.pin_42, LED2.cathode
  N5: J1.pin2, Mod1.pin_17
  N6: Mod1.pin_19, R1.Pin_1
  N7: Mod1.pin_20, R2.Pin_1
  N8: LED2.anode, R2.Pin_0

custom parts:
  Raspberry Pi Pico W: Raspberry Pi Pico W. Based around the RP2040 microcontroller the Pico W is a low cost microcontroller device bringing Raspberry Pi quality, cost, and easy of use to the microcontroller space. The areas marked KEEPOUT in pcb silkscreen should not have traces running through them to avoid shorts on a soldered in module!
